// Logisim project adder-1.circ as structural Verilog: 17 circuits, main circuit main
module main (
);

  wire button_1_out, clock_1_out, not_1_out, not_2_out, Overflow_q, uc_unit_control_1_clk_ac,
       uc_unit_control_1_clk_ir, uc_unit_control_1_clk_pc, uc_unit_control_1_clk_ram,
       \uc_unit_control_1_direção , uc_unit_control_1_e, uc_unit_control_1_load, uc_unit_control_1_r___w,
       uc_unit_control_1_rst_pc, ula_1_overflow, ula_1_zero, Zero_q;
  wire [2:0] \uc_unit_control_1_operação ;
  wire [3:0] counter_1_q, mux_21_1_out_4, ram_1_data, registrador_ac_1_q, \uc_unit_control_1_b_endereços ,
       uc_unit_control_1_dados, uc_unit_control_1_operando, \ula_1_saída ;
  wire [7:0] ir_1_out_3, rom_1_data;

  not not_1 (not_1_out, uc_unit_control_1_load);
  Button button_1 (.out(button_1_out));
  Clock clock_1 (.out(clock_1_out));
  IR ir_1 (.out_3(ir_1_out_3), .in_2(rom_1_data), .Clock(uc_unit_control_1_clk_ir));
  ROM #(.addrWidth(4)) rom_1 (.addr(counter_1_q), .data(rom_1_data));  // open: sel
  Counter #(.width(4), .max('hf)) counter_1 (
    .load(uc_unit_control_1_load), .D(uc_unit_control_1_dados), .count(not_1_out), .Q(counter_1_q),
    .clk(uc_unit_control_1_clk_pc), .clr(uc_unit_control_1_rst_pc));  // open: carry
  UC___Unit_control uc_unit_control_1 (
    .\B_Endereços (\uc_unit_control_1_b_endereços ), .Operando(uc_unit_control_1_operando),
    .\Direção (\uc_unit_control_1_direção ), .E(uc_unit_control_1_e),
    .\Operação (\uc_unit_control_1_operação ), .\Instrução (ir_1_out_3), .CLK_RAM(uc_unit_control_1_clk_ram),
    .CLK_AC(uc_unit_control_1_clk_ac), .CLK_PC(uc_unit_control_1_clk_pc), .CLK_IR(uc_unit_control_1_clk_ir),
    .CLOCK(clock_1_out), .RESET(button_1_out), .RST_PC(uc_unit_control_1_rst_pc), .Zero(Zero_q),
    .Overflow(Overflow_q), .R___W(uc_unit_control_1_r___w), .Load(uc_unit_control_1_load),
    .Dados(uc_unit_control_1_dados));
  Mux_21 mux_21_1 (
    .E(uc_unit_control_1_operando), .Controle(uc_unit_control_1_e), .D(ram_1_data), .out_4(mux_21_1_out_4));
  // Probe on registrador_ac_1_q
  ULA ula_1 (
    .D(\uc_unit_control_1_direção ), .A(registrador_ac_1_q), .B(mux_21_1_out_4),
    .in_4(\uc_unit_control_1_operação ), .\SAÍDA (\ula_1_saída ), .ZERO(ula_1_zero), .OVERFLOW(ula_1_overflow));
  Registrador_AC registrador_ac_1 (.Q(registrador_ac_1_q), .D(\ula_1_saída ), .CLOCk(uc_unit_control_1_clk_ac));
  // Probe on mux_21_1_out_4
  RAM #(.addrWidth(4), .dataWidth(4)) ram_1 (
    .addr(\uc_unit_control_1_b_endereços ), .data(ram_1_data), .clk(uc_unit_control_1_clk_ram),
    .ld(uc_unit_control_1_r___w));  // open: sel, clr
  not not_2 (not_2_out, uc_unit_control_1_r___w);
  D_Flip_Flop Overflow (
    .clk(uc_unit_control_1_clk_ac), .D(ula_1_overflow), .Q(Overflow_q));  // open: Qn, preset, en, reset
  D_Flip_Flop Zero (.clk(uc_unit_control_1_clk_ac), .D(ula_1_zero), .Q(Zero_q));  // open: Qn, preset, en, reset
  Buffer buffer_1 (.B(registrador_ac_1_q), .Controle(not_2_out), .S(ram_1_data));

  // Notes on the sheet:
  //   contents of rom_1 (hex, n*v repeats v):
  //   0 f0 0 1 f1 10 31 d0 f2 11 f0 12 f1 e4
endmodule

module UC___Unit_control (
  input  [7:0] \Instrução ,
  input  CLOCK,
  input  RESET,
  input  Zero,
  input  Overflow,
  output [3:0] Dados,
  output CLK_RAM,
  output [3:0] \B_Endereços ,
  output CLK_IR,
  output [3:0] Operando,
  output CLK_AC,
  output \Direção ,
  output RST_PC,
  output CLK_PC,
  output E,
  output [2:0] \Operação ,
  output R___W,
  output Load
);

  wire GoTo_out, JP0_out, JPZ_out, nand_1_out;
  wire [1:0] counter_1_q;

  and Storage (R___W, \Instrução [7], \Instrução [6], \Instrução [5], \Instrução [4], CLK_AC);
  Counter #(.width(2), .max('h3)) counter_1 (.Q(counter_1_q), .clk(CLOCK), .clr(RESET));  // open: load, D, count, carry
  and GoTo (GoTo_out, \Instrução [7], \Instrução [6], \Instrução [5], \Instrução [4], CLK_PC);
  and and_1 (CLK_IR, ~counter_1_q[0], ~counter_1_q[1]);  // AND_Gate
  and and_2 (CLK_PC, counter_1_q[0], ~counter_1_q[1]);  // AND_Gate
  and JP0 (JP0_out, \Instrução [7], \Instrução [6], \Instrução [5], \Instrução [4], CLK_PC, Overflow);
  or or_1 (Load, GoTo_out, JP0_out, JPZ_out);
  and and_3 (CLK_AC, ~counter_1_q[0], counter_1_q[1]);  // AND_Gate
  and and_4 (CLK_RAM, counter_1_q[0], counter_1_q[1]);
  and JPZ (JPZ_out, \Instrução [7], \Instrução [6], \Instrução [5], \Instrução [4], CLK_PC, Zero);
  and and_5 (E, \Instrução [4], nand_1_out);
  nand nand_1 (nand_1_out, \Instrução [7], ~\Instrução [6], \Instrução [5]);  // NAND_Gate

  assign \B_Endereços  = \Instrução [3:0];
  assign Dados = \Instrução [3:0];
  assign \Direção  = \Instrução [4];
  assign Operando = \Instrução [3:0];
  assign \Operação  = \Instrução [7:5];
  assign RST_PC = RESET;
endmodule

module ULA (
  input  D,
  input  [3:0] A,
  input  [3:0] B,
  input  [2:0] in_4,
  output OVERFLOW,
  output [3:0] \SAÍDA ,
  output ZERO
);

  wire adder_4_1_overflow, and_1_out, and_2_out, codificador_1_s0, codificador_1_s1, codificador_1_s2,
       codificador_1_s3, codificador_1_s4, codificador_1_s5, codificador_1_s6, codificador_1_s7, not_1_out,
       sub_4_1_out_3;
  wire [3:0] adder_4_1_out_4, buffer_right_1_s, or_gate_1_out_3, rot_l_1_abcd_2, rot_r_1_abcd_2,
       sub_4_1_out_4;

  Codificador codificador_1 (
    .S0(codificador_1_s0), .S1(codificador_1_s1), .S2(codificador_1_s2), .S3(codificador_1_s3),
    .S4(codificador_1_s4), .S5(codificador_1_s5), .S6(codificador_1_s6), .S7(codificador_1_s7), .in_1(in_4));
  Buffer buffer_1 (.B(B), .Controle(codificador_1_s0), .S(\SAÍDA ));
  nor nor_1 (ZERO, codificador_1_s7, codificador_1_s6, \SAÍDA [3], \SAÍDA [2], \SAÍDA [1], \SAÍDA [0]);
  adder_4 adder_4_1 (.OVERFLOW(adder_4_1_overflow), .out_4(adder_4_1_out_4), .in_2(B), .in_1(A));
  Buffer buffer_2 (.B(adder_4_1_out_4), .Controle(codificador_1_s1), .S(\SAÍDA ));
  and and_1 (and_1_out, codificador_1_s1, adder_4_1_overflow);
  and and_2 (and_2_out, sub_4_1_out_3, codificador_1_s2);
  or or_1 (OVERFLOW, and_1_out, and_2_out);
  Sub_4 sub_4_1 (.in_1(A), .out_3(sub_4_1_out_3), .in_2(B), .out_4(sub_4_1_out_4));
  Buffer buffer_3 (.B(sub_4_1_out_4), .Controle(codificador_1_s2), .S(\SAÍDA ));
  OR_gate or_gate_1 (.in_1(A), .in_2(B), .out_3(or_gate_1_out_3));
  Buffer buffer_4 (.B(or_gate_1_out_3), .Controle(codificador_1_s3), .S(\SAÍDA ));
  Buffer_Inversor buffer_inversor_1 (.B(B), .Controle(codificador_1_s4), .S(\SAÍDA ));
  rot_L rot_l_1 (.ABCD(A), .abcd_2(rot_l_1_abcd_2), .XY(B[1:0]));
  rot_R rot_r_1 (.ABCD(A), .abcd_2(rot_r_1_abcd_2), .XY(B[1:0]));
  not not_1 (not_1_out, D);
  Buffer__right buffer_right_1 (.B(rot_r_1_abcd_2), .Controle(not_1_out), .S(buffer_right_1_s));
  Buffer__right buffer_right_2 (.B(rot_l_1_abcd_2), .Controle(D), .S(buffer_right_1_s));
  Buffer buffer_5 (.B(buffer_right_1_s), .Controle(codificador_1_s5), .S(\SAÍDA ));
endmodule

module Buffer (
  input  [3:0] B,
  input  Controle,
  output [3:0] S
);

  assign S[3] = Controle ? B[3] : 1'bz;  // Controlled_Buffer controlled_buffer_1
  assign S[1] = Controle ? B[1] : 1'bz;  // Controlled_Buffer controlled_buffer_2
  assign S[2] = Controle ? B[2] : 1'bz;  // Controlled_Buffer controlled_buffer_3
  assign S[0] = Controle ? B[0] : 1'bz;  // Controlled_Buffer controlled_buffer_4
endmodule

module Buffer__right (
  input  [3:0] B,
  input  Controle,
  output [3:0] S
);

  assign S[3] = Controle ? B[3] : 1'bz;  // Controlled_Buffer controlled_buffer_1
  assign S[1] = Controle ? B[1] : 1'bz;  // Controlled_Buffer controlled_buffer_2
  assign S[2] = Controle ? B[2] : 1'bz;  // Controlled_Buffer controlled_buffer_3
  assign S[0] = Controle ? B[0] : 1'bz;  // Controlled_Buffer controlled_buffer_4

  // Notes on the sheet:
  //   (FIz por motivos estéticos apenas)
  //   Idêntico ao buffer normal, mas com a porta de controle do lado direito.
endmodule

module Buffer_Inversor (
  input  [3:0] B,
  input  Controle,
  output [3:0] S
);

  assign S[1] = Controle ? ~B[1] : 1'bz;  // Controlled_Inverter controlled_inverter_1
  assign S[3] = Controle ? ~B[3] : 1'bz;  // Controlled_Inverter controlled_inverter_2
  assign S[2] = Controle ? ~B[2] : 1'bz;  // Controlled_Inverter controlled_inverter_3
  assign S[0] = Controle ? ~B[0] : 1'bz;  // Controlled_Inverter controlled_inverter_4
endmodule

module Codificador (
  input  [2:0] in_1,
  output S0,
  output S1,
  output S2,
  output S3,
  output S4,
  output S5,
  output S6,
  output S7
);

  wire not_1_out, not_2_out, not_3_out, not_4_out, not_5_out, not_6_out, not_7_out, not_8_out, not_9_out,
       not_10_out, not_11_out, not_12_out;

  not not_1 (not_1_out, in_1[2]);
  not not_2 (not_2_out, in_1[1]);
  not not_3 (not_3_out, in_1[0]);
  not not_4 (not_4_out, in_1[2]);
  not not_5 (not_5_out, in_1[1]);
  not not_6 (not_6_out, in_1[2]);
  not not_7 (not_7_out, in_1[0]);
  not not_8 (not_8_out, in_1[2]);
  not not_9 (not_9_out, in_1[1]);
  not not_10 (not_10_out, in_1[0]);
  not not_11 (not_11_out, in_1[1]);
  not not_12 (not_12_out, in_1[0]);
  and and_1 (S7, in_1[2], in_1[1], in_1[0]);
  and and_2 (S0, not_1_out, not_2_out, not_3_out);
  and and_3 (S1, not_4_out, not_5_out, in_1[0]);
  and and_4 (S2, not_6_out, in_1[1], not_7_out);
  and and_5 (S3, not_8_out, in_1[1], in_1[0]);
  and and_6 (S4, in_1[2], not_9_out, not_10_out);
  and and_7 (S5, in_1[2], not_11_out, in_1[0]);
  and and_8 (S6, in_1[2], in_1[1], not_12_out);
endmodule

module adder_4 (
  input  [3:0] in_1,
  input  [3:0] in_2,
  output OVERFLOW,
  output [3:0] out_4
);

  wire adder_1_2_c_out, adder_1_3_c_out, adder_1_4_c_out;

  Adder_1 adder_1_1 (.A(in_2[3]), .B(in_1[3]), .C_in(adder_1_2_c_out), .S(out_4[3]), .C_out(OVERFLOW));
  Adder_1 adder_1_2 (.A(in_2[2]), .B(in_1[2]), .C_in(adder_1_3_c_out), .S(out_4[2]), .C_out(adder_1_2_c_out));
  Adder_1 adder_1_3 (.A(in_2[1]), .B(in_1[1]), .C_in(adder_1_4_c_out), .S(out_4[1]), .C_out(adder_1_3_c_out));
  Adder_1 adder_1_4 (.A(in_2[0]), .B(in_1[0]), .C_in(1'b0), .S(out_4[0]), .C_out(adder_1_4_c_out));
endmodule

module Adder_1 (
  input  A,
  input  B,
  input  C_in,
  output S,
  output C_out
);

  wire and_1_out, and_2_out, xor_1_out;

  xor xor_1 (xor_1_out, A, B);
  and and_1 (and_1_out, B, A);
  and and_2 (and_2_out, C_in, xor_1_out);
  xor xor_2 (S, xor_1_out, C_in);
  or or_1 (C_out, and_2_out, and_1_out);
endmodule

module Sub_4 (
  input  [3:0] in_1,
  input  [3:0] in_2,
  output out_3,
  output [3:0] out_4
);

  wire sub_1_2_c_out, sub_1_3_c_out, sub_1_4_c_out;

  Sub_1 sub_1_1 (.A(in_1[3]), .B(in_2[3]), .S(out_4[3]), .C_in(sub_1_2_c_out), .C_out(out_3));
  Sub_1 sub_1_2 (.A(in_1[2]), .B(in_2[2]), .S(out_4[2]), .C_in(sub_1_3_c_out), .C_out(sub_1_2_c_out));
  Sub_1 sub_1_3 (.A(in_1[1]), .B(in_2[1]), .S(out_4[1]), .C_in(sub_1_4_c_out), .C_out(sub_1_3_c_out));
  Sub_1 sub_1_4 (.A(in_1[0]), .B(in_2[0]), .S(out_4[0]), .C_in(1'b0), .C_out(sub_1_4_c_out));
endmodule

module Sub_1 (
  input  A,
  input  B,
  input  C_in,
  output S,
  output C_out
);

  wire and_1_out, and_2_out, not_1_out, not_2_out, xor_1_out;

  not not_1 (not_1_out, A);
  xor xor_1 (xor_1_out, A, B);
  not not_2 (not_2_out, xor_1_out);
  and and_1 (and_1_out, B, not_1_out);
  and and_2 (and_2_out, C_in, not_2_out);
  xor xor_2 (S, xor_1_out, C_in);
  or or_1 (C_out, and_2_out, and_1_out);
endmodule

module rot_L (
  input  [1:0] XY,
  input  [3:0] ABCD,
  output [3:0] abcd_2
);

  wire and_1_out, and_2_out, and_3_out, and_4_out, and_5_out, and_6_out, and_7_out, and_8_out, and_9_out;

  and and_1 (and_1_out, ~XY[1], ~XY[0], ABCD[3]);  // AND_Gate
  and and_2 (and_2_out, ~XY[1], XY[0], ABCD[2]);  // AND_Gate
  and and_3 (and_3_out, XY[1], ~XY[0], ABCD[1]);  // AND_Gate
  and and_4 (and_4_out, XY[1], XY[0], ABCD[0]);
  and and_5 (and_5_out, ~XY[1], ~XY[0], ABCD[2]);  // AND_Gate
  and and_6 (and_6_out, ~XY[1], XY[0], ABCD[1]);  // AND_Gate
  and and_7 (and_7_out, XY[1], ~XY[0], ABCD[0]);  // AND_Gate
  and and_8 (and_8_out, ~XY[1], ~XY[0], ABCD[1]);  // AND_Gate
  and and_9 (and_9_out, ~XY[1], XY[0], ABCD[0]);  // AND_Gate
  and and_10 (abcd_2[0], ~XY[1], ~XY[0], ABCD[0]);  // AND_Gate
  or or_1 (abcd_2[3], and_1_out, and_2_out, and_3_out, and_4_out);
  or or_2 (abcd_2[2], and_5_out, and_6_out, and_7_out);
  or or_3 (abcd_2[1], and_8_out, and_9_out);
endmodule

module rot_R (
  input  [1:0] XY,
  input  [3:0] ABCD,
  output [3:0] abcd_2
);

  wire and_1_out, and_2_out, and_3_out, and_4_out, and_5_out, and_6_out, and_7_out, and_8_out, and_9_out;

  and and_1 (and_1_out, ~XY[1], ~XY[0], ABCD[0]);  // AND_Gate
  and and_2 (and_2_out, ~XY[1], XY[0], ABCD[1]);  // AND_Gate
  and and_3 (and_3_out, XY[1], ~XY[0], ABCD[2]);  // AND_Gate
  and and_4 (and_4_out, XY[1], XY[0], ABCD[3]);
  and and_5 (and_5_out, ~XY[1], ~XY[0], ABCD[1]);  // AND_Gate
  and and_6 (and_6_out, ~XY[1], XY[0], ABCD[2]);  // AND_Gate
  and and_7 (and_7_out, XY[1], ~XY[0], ABCD[3]);  // AND_Gate
  and and_8 (and_8_out, ~XY[1], ~XY[0], ABCD[2]);  // AND_Gate
  and and_9 (and_9_out, ~XY[1], XY[0], ABCD[3]);  // AND_Gate
  and and_10 (abcd_2[3], ~XY[1], ~XY[0], ABCD[3]);  // AND_Gate
  or or_1 (abcd_2[0], and_1_out, and_2_out, and_3_out, and_4_out);
  or or_2 (abcd_2[1], and_5_out, and_6_out, and_7_out);
  or or_3 (abcd_2[2], and_8_out, and_9_out);
endmodule

module OR_gate (
  input  [3:0] in_1,
  input  [3:0] in_2,
  output [3:0] out_3
);

  or or_1 (out_3[3], in_1[3], in_2[3]);
  or or_2 (out_3[2], in_1[2], in_2[2]);
  or or_3 (out_3[1], in_1[1], in_2[1]);
  or or_4 (out_3[0], in_1[0], in_2[0]);
endmodule

module Registrador_AC (
  input  CLOCk,
  input  [3:0] D,
  output [3:0] Q
);

  D_Flip_Flop d_ff_1 (.clk(CLOCk), .D(D[3]), .Q(Q[3]));  // open: Qn, preset, en, reset
  D_Flip_Flop d_ff_2 (.clk(CLOCk), .D(D[2]), .Q(Q[2]));  // open: Qn, preset, en, reset
  D_Flip_Flop d_ff_3 (.clk(CLOCk), .D(D[1]), .Q(Q[1]));  // open: Qn, preset, en, reset
  D_Flip_Flop d_ff_4 (.clk(CLOCk), .D(D[0]), .Q(Q[0]));  // open: Qn, preset, en, reset
endmodule

module Mux_21 (
  input  [3:0] E,
  input  [3:0] D,
  input  Controle,
  output [3:0] out_4
);

  wire not_1_out;

  Buffer buffer_1 (.B(E), .Controle(not_1_out), .S(out_4));
  not not_1 (not_1_out, Controle);
  Buffer buffer_2 (.B(D), .Controle(Controle), .S(out_4));
endmodule

module IR (
  input  Clock,
  input  [7:0] in_2,
  output [7:0] out_3
);

  D_Flip_Flop d_ff_1 (.clk(Clock), .D(in_2[7]), .Q(out_3[7]));  // open: Qn, preset, en, reset
  D_Flip_Flop d_ff_2 (.clk(Clock), .D(in_2[6]), .Q(out_3[6]));  // open: Qn, preset, en, reset
  D_Flip_Flop d_ff_3 (.clk(Clock), .D(in_2[5]), .Q(out_3[5]));  // open: Qn, preset, en, reset
  D_Flip_Flop d_ff_4 (.clk(Clock), .D(in_2[4]), .Q(out_3[4]));  // open: Qn, preset, en, reset
  D_Flip_Flop d_ff_5 (.clk(Clock), .D(in_2[3]), .Q(out_3[3]));  // open: Qn, preset, en, reset
  D_Flip_Flop d_ff_6 (.clk(Clock), .D(in_2[2]), .Q(out_3[2]));  // open: Qn, preset, en, reset
  D_Flip_Flop d_ff_7 (.clk(Clock), .D(in_2[1]), .Q(out_3[1]));  // open: Qn, preset, en, reset
  D_Flip_Flop d_ff_8 (.clk(Clock), .D(in_2[0]), .Q(out_3[0]));  // open: Qn, preset, en, reset
endmodule
